# Fritzing sketch Robit_MK2 (saved by Fritzing 0.9.3b)
breadboards: 4

parts:
  MH-ET_LIVE_ESP32_DEVKIT1 = MH-ET LIVE ESP32 DEVKIT 38 pins
  Pololu_A1 = Pololu A4988 [package=SO16]
  M2 = Stepper Motor - Bipolar
  12V = 12V BatPack [package="12V BatPack"]
  U3 = Mini-360 DC-DC Buck converter [package=THT]
  U4 = MinIMU-9
  M1 = Stepper Motor - Bipolar
  Pololu_A2 = Pololu A4988 [package=SO16]
  R1 = Resistor [tolerance=±5% resistance=1k package="0402 [SMD]"]
  R2 = Resistor [tolerance=±5% resistance=1k package="0402 [SMD]"]
  LED3 = LED - 3mm [color="Red (633nm)" package="3 mm [THT]"]
  LED4 = LED - 3mm [color="Green (555nm)" package="3 mm [THT]"]
  J1 = Basic Servo
  J2 = Basic Servo
  hc-sr1 = hc-sr04
  C2 = Electrolytic Capacitor [capacitance=100µF voltage=35V package="200 mil [THT, electrolytic]"]
  C3 = Electrolytic Capacitor [capacitance=100µF voltage=35V package="200 mil [THT, electrolytic]"]

nets:
  VDD: MH-ET_LIVE_ESP32_DEVKIT1.3V3, Pololu_A1.MS1, Pololu_A1.MS2, Pololu_A1.VDD, Pololu_A2.MS1, Pololu_A2.MS2, Pololu_A2.VDD
  N1: MH-ET_LIVE_ESP32_DEVKIT1.IO33, J1.pulse
  N2: MH-ET_LIVE_ESP32_DEVKIT1.IO25, Pololu_A1.DIR
  N3: MH-ET_LIVE_ESP32_DEVKIT1.IO26, Pololu_A1.STEP
  N4: MH-ET_LIVE_ESP32_DEVKIT1.IO27, Pololu_A2.DIR
  N5: MH-ET_LIVE_ESP32_DEVKIT1.IO14, Pololu_A2.STEP
  N6: MH-ET_LIVE_ESP32_DEVKIT1.IO12, Pololu_A1.ENABLE, Pololu_A2.ENABLE
  GND: MH-ET_LIVE_ESP32_DEVKIT1.GND, Pololu_A1.GND, 12V.-, U3.IN-, U3.OUT-, U4.GND, Pololu_A2.GND, LED3.cathode, LED4.cathode, J1.gnd, J2.gnd, hc-sr1.GND, C2.-, C3.-
  N7: MH-ET_LIVE_ESP32_DEVKIT1.IO13, J2.pulse
  VCC: MH-ET_LIVE_ESP32_DEVKIT1.5V, U3.OUT+, U4.VIN, J1.vcc, J2.vcc, hc-sr1.VCC
  N8: MH-ET_LIVE_ESP32_DEVKIT1.IO22, U4.SCL
  N9: MH-ET_LIVE_ESP32_DEVKIT1.IO21, U4.SDA
  N10: MH-ET_LIVE_ESP32_DEVKIT1.IO18, hc-sr1.Echo
  N11: MH-ET_LIVE_ESP32_DEVKIT1.IO5, hc-sr1.Trig
  N12: MH-ET_LIVE_ESP32_DEVKIT1.IO0, R2.Pin_0
  N13: MH-ET_LIVE_ESP32_DEVKIT1.IO2, R1.Pin_0
  N14: Pololu_A1.RESET, Pololu_A1.SLEEP
  N15: Pololu_A1.1B, M1.D
  N16: Pololu_A1.1A, M1.B
  N17: Pololu_A1.2A, M1.C
  N18: Pololu_A1.2B, M1.A
  N19: Pololu_A1.VMOT, 12V.12V_BatPack, U3.IN+, Pololu_A2.VMOT, C2.+, C3.+
  N20: M2.A, Pololu_A2.2B
  N21: M2.C, Pololu_A2.2A
  N22: M2.B, Pololu_A2.1A
  N23: M2.D, Pololu_A2.1B
  N24: Pololu_A2.RESET, Pololu_A2.SLEEP
  N25: R1.Pin_1, LED3.anode
  N26: R2.Pin_1, LED4.anode

notes:
  12V
  5V
  RAISEUP SERVOS
  US SENSOR
  Pololu IMU v4
  INDICATOR LEDs
  5V (ESP32 PWR)

custom parts:
  MH-ET LIVE ESP32 DEVKIT 38 pins: http://mh.nodebb.com/topic/2/mh-et-live-esp32-devkit
  12V BatPack: 2000mAh Lipo-battery
  Mini-360 DC-DC Buck converter: Mini-360 DC-DC Buck converter. Tiny buck step down voltage converter, input voltage 4.75 to 23V output 1 to 17V adjustable. Available from ebay and the like.
  MinIMU-9: MinIMU-9 9-axis compass/accelerometer/gyro. I2C interface.
  hc-sr04: This is a HC-SR04 Distance Sensor
